# Fritzing sketch Smart Lock (saved by Fritzing 0.9.3b)
breadboards: 1

parts:
  U1 = LuaNode32 / ESP32 [part_number=ESP32S-PIN30]
  元件1 = RFID-RC522-v2
  J1 = Basic Servo

nets:
  GND: U1.GND, 元件1.GND
  3V3: U1.3V3, 元件1.3.3V
  N1: U1.D4, J1.pulse
  N2: U1.D18, 元件1.SCK
  N3: U1.D19, 元件1.MISO
  N4: U1.D21, 元件1.SDA
  N5: U1.D22, 元件1.RST
  N6: U1.D23, 元件1.MOSI

custom parts:
  LuaNode32 / ESP32: New Image for LuaNode32 DOIT ESP32 DEVKIT V1. Base parts from LuaNode32 / ESP32 ESP32 based LuaNode32 by G.Noorlander DOIT Esp32 DevKit v1 (30 pins long, 11 pins width) by Werner Rothschopf (modified by vanepp Dec 2018)
  RFID-RC522-v2: A simple China made RFID-RC522 Reader; do check the pin labels, as this is a MFRC522 based clone.
